# Fritzing sketch schematic (saved by Fritzing 0.9.3b)
breadboards: 1

parts:
  Part2 = RFID-RC522-v3
  Part3 = Arduino Pro Mini (5V)
  R1 = Resistor [tolerance=±5% resistance=1k package="0402 [SMD]"]
  R3 = Resistor [tolerance=±5% resistance=1k package="0402 [SMD]"]
  R2 = Resistor [tolerance=±5% resistance=1k package="0402 [SMD]"]

nets:
  N1: Part2.SDA, Part3.D10
  N2: Part2.SCK, Part3.SCK
  N3: Part2.MOSI, Part3.MOSI
  N4: Part2.MISO, Part3.MISO
  GND: Part2.GND, Part3.GND, R1.Pin_0
  N5: Part2.RST, Part3.D6
  N6: Part2.3.3V, R1.Pin_1, R2.Pin_0
  N7: Part3.VCC, R3.Pin_0
  N8: R3.Pin_1, R2.Pin_1

custom parts:
  RFID-RC522-v3: A simple China made RFID-RC522 Reader (6x4 cm); do check the pin labels, as this is a MFRC522 based clone.
